# Fritzing sketch mcp_complete_pi (saved by Fritzing 0.9.3b)
breadboards: 2

parts:
  Raspberry_Pi_1 = Raspberry Pi 3 [part_number=RPI-3-V1.2]
  LED1 = LEDs [package=led10mm]
  U1 = NodeMCU V1.0  # not connected
  LED2 = LEDs [package=led10mm]  # not connected
  U2 = POT [package=pot_mammoth]  # not connected
  MCP1 = MCP3008 [part_number=MCP3008 package="DIP (Dual Inline) [THT]"]
  U3 = POT [package=pot_mammoth]
  R1 = Photocell (LDR) [package=THT]
  R2 = Resistor [tolerance=±5% resistance=220 package=THT]

nets:
  3V3: Raspberry_Pi_1.3v3, Raspberry_Pi_1.3V3, MCP1.VREF, MCP1.VDD, U3.E, R1.pin_0
  N1: Raspberry_Pi_1.GIPO10, MCP1.MOSI
  N2: Raspberry_Pi_1.GIPO9, MCP1.MISO
  N3: Raspberry_Pi_1.GIPO11, MCP1.SCLK
  N4: Raspberry_Pi_1.GIPO21, LED1.A
  N5: Raspberry_Pi_1.GIPO8, MCP1.CE
  N6: Raspberry_Pi_1.GND, LED1.C, MCP1.DGND, MCP1.AGND, U3.S, R2.Pin_1
  N7: MCP1.CH0, U3.A
  N8: MCP1.CH1, R1.pin_1, R2.Pin_0

custom parts:
  NodeMCU V1.0: ESP8266 based NodeMCU V1.0
  MCP3008: 10-bit ADC for Raspberry Pi
